// Logisim project TN1.circ as structural Verilog: 1 circuit, main circuit main
module main (
  input  A,
  input  B,
  input  C,
  output ONE,
  output TWO,
  output THREE,
  output CHAIN,
  output FIVE,
  output SIX,
  output SEVEN
);

  wire nand_1_out;

  not not_1 (ONE, A);
  and and_1 (TWO, A, B);
  or or_1 (THREE, A, B);
  nand nand_1 (nand_1_out, A, B);
  nor nor_1 (FIVE, A, B);
  ExactlyOne xor_1 (.out(SIX), .in0(A), .in1(C), .in2(B));
  xnor xnor_1 (SEVEN, A, B);
  nand nand_2 (CHAIN, nand_1_out, C);
endmodule
