// Logisim project TN2.circ as structural Verilog: 1 circuit, main circuit main
module main (
  input  x,
  input  y,
  input  z,
  output EQ4,
  output EQ1,
  output EQ2,
  output EQ3,
  output EQ5
);

  wire and_1_out, and_2_out, and_3_out, and_4_out, and_5_out, and_6_out, nand_1_out, nor_1_out, not_1_out,
       not_2_out, not_3_out, not_4_out, or_1_out, or_2_out, or_3_out, or_4_out, or_5_out, or_6_out;

  not not_1 (not_1_out, x);
  not not_2 (not_2_out, x);
  not not_3 (not_3_out, y);
  not not_4 (not_4_out, x);
  and and_1 (and_1_out, not_1_out, y);
  and and_2 (and_2_out, y, z);
  or or_1 (or_1_out, x, y);
  or or_2 (or_2_out, x, z);
  and and_3 (and_3_out, not_4_out, y);
  or or_3 (or_3_out, and_1_out, x);
  and and_4 (and_4_out, not_2_out, not_3_out);
  and and_5 (and_5_out, not_2_out, not_3_out);
  or or_4 (or_4_out, and_2_out, x);
  and and_6 (and_6_out, or_1_out, or_2_out);
  or or_5 (or_5_out, and_3_out, x);
  or or_6 (or_6_out, y, x);
  nor nor_1 (nor_1_out, x, y);
  nand nand_1 (nand_1_out, x, y);
  xnor xnor_1 (EQ4, or_3_out, x);
  xnor xnor_2 (EQ1, nor_1_out, and_4_out);
  xnor xnor_3 (EQ2, nand_1_out, and_5_out);
  xnor xnor_4 (EQ3, or_4_out, and_6_out);
  xnor xnor_5 (EQ5, or_5_out, or_6_out);
endmodule
