// Logisim project TN3.circ as structural Verilog: 1 circuit, main circuit main
module main (
  input  NA,
  input  B,
  input  NB,
  input  C,
  input  NC,
  input  D,
  input  ND,
  input  A,
  output F
);

  wire and_1_out, and_2_out, and_3_out, and_4_out, and_5_out, and_6_out;

  and and_1 (and_1_out, NA, NB, C, ND);
  and and_2 (and_2_out, NC, B, D, A);
  and and_3 (and_3_out, NA, C, D, NB);
  and and_4 (and_4_out, NA, D, B, NC);
  and and_5 (and_5_out, NA, B, C, D);
  and and_6 (and_6_out, NB, C, D, A);
  or or_1 (F, and_1_out, and_3_out, and_4_out, and_5_out, and_6_out, and_2_out);
endmodule
