// Logisim project TN4.circ as structural Verilog: 1 circuit, main circuit main
module main (
  input  A,
  input  B,
  input  C,
  input  D,
  output EQ1,
  output EQ2
);

  wire and_1_out, and_2_out, and_3_out, and_4_out, and_5_out, and_6_out, and_7_out, and_8_out, and_9_out,
       and_10_out, F_can_out, F_pos_out, F_sop_out, not_1_out, not_2_out, not_3_out, not_4_out, or_1_out,
       or_2_out, or_3_out, or_4_out;

  not not_1 (not_1_out, A);
  not not_2 (not_2_out, B);
  not not_3 (not_3_out, C);
  not not_4 (not_4_out, D);
  and and_1 (and_1_out, not_1_out, not_2_out, not_4_out, C);
  and and_2 (and_2_out, not_1_out, not_2_out, C, D);
  and and_3 (and_3_out, not_1_out, B, D, not_3_out);
  and and_4 (and_4_out, not_1_out, B, C, D);
  and and_5 (and_5_out, not_2_out, A, C, D);
  and and_6 (and_6_out, not_3_out, A, C, D);
  and and_7 (and_7_out, not_1_out, not_2_out, C);
  and and_8 (and_8_out, B, not_3_out, D);
  and and_9 (and_9_out, not_1_out, B, D);
  and and_10 (and_10_out, not_2_out, C, D);
  or or_1 (or_1_out, not_1_out, not_2_out, not_3_out);
  or or_2 (or_2_out, C, D);
  or or_3 (or_3_out, B, C);
  or or_4 (or_4_out, not_2_out, D);
  or F_can (F_can_out, and_1_out, and_2_out, and_3_out, and_4_out, and_5_out, and_6_out);
  or F_sop (F_sop_out, and_7_out, and_8_out, and_9_out, and_10_out);
  and F_pos (F_pos_out, or_1_out, or_2_out, or_3_out, or_4_out);
  xnor xnor_1 (EQ1, F_can_out, F_sop_out);
  xnor xnor_2 (EQ2, F_can_out, F_pos_out);
endmodule
